# Fritzing sketch arduino_reaktionsspiel (saved by Fritzing 0.9.3b)
breadboards: 1

parts:
  LED1 = LED - 5mm [color="Red (633nm)" package="5 mm [THT]"]
  LED2 = LED - 5mm [color="Green (560nm)" package="5 mm [THT]"]
  LED3 = LED - 5mm [color="Green (560nm)" package="5 mm [THT]"]
  R1 = Resistor [tolerance=±5% resistance=220 package=THT]
  R2 = Resistor [tolerance=±5% resistance=220 package=THT]
  R3 = Resistor [tolerance=±5% resistance=220 package=THT]
  S1 = Pushbutton [package="[THT]"]
  S2 = Pushbutton [package="[THT]"]
  R4 = Resistor [tolerance=±5% resistance=220 package=THT]
  R5 = Resistor [tolerance=±5% resistance=220 package=THT]
  Bauteil1 = Arduino Uno (Rev3)

nets:
  N1: LED1.cathode, R1.Pin_1
  N2: LED1.anode, Bauteil1.D6_PWM
  N3: LED2.cathode, R2.Pin_1
  N4: LED2.anode, Bauteil1.D2
  N5: LED3.cathode, R3.Pin_1
  N6: LED3.anode, Bauteil1.D4
  N7: R1.Pin_0, R2.Pin_0, R3.Pin_0, S1.Pin_1, S1.Pin_2, S2.Pin_1, S2.Pin_2, R4.Pin_0, R5.Pin_0, Bauteil1.GND
  N8: S1.Pin_3, S1.Pin_4, R4.Pin_1, Bauteil1.D7
  N9: S2.Pin_3, S2.Pin_4, R5.Pin_1, Bauteil1.D5_PWM
